// Logisim project my_CPU.circ as structural Verilog
module main (
  output [4:0] out_1
);

  wire CLK, CLLK, OE_RAM, S_AB_ALU, S_I_MD, S_MA, S_O_MD, WE_A_ALU, WE_A_op_B, WE_B_ALU, WE_GRG, WE_IR,
       WE_MA, WE_MD, WE_PC, WE_RAM;
  wire [1:0] S_I_PC, S_r12d_A_GRG;
  wire [2:0] funct3;
  wire [3:0] op_ALU;
  wire [4:0] instruction_stuct_decoder_1_rd, instruction_stuct_decoder_1_rs1, instruction_stuct_decoder_1_rs2;
  wire [6:0] funct7, opcode;
  wire [11:0] instruction_stuct_decoder_1_i_11_0;
  wire [31:0] A_RAM, adder_1_out, adder_2_out, adder_3_out, alu_complete_1_out_4, demultiplexer_1_out0,
       demultiplexer_1_out1, demultiplexer_2_out1, general_register_group_1_data_output, I_RAM, imm_Addr,
       IR_q, MD_q, multiplexer_2_out, multiplexer_3_out, O_RAM, pc_complete_1_pc_val, pc_reset_val,
       register_1_q, register_2_q, register_3_q;

  Adder #(.width(32)) adder_1 (.a(pc_complete_1_pc_val), .b(32'h4), .out(adder_1_out), .cin(1'b0));  // open: cout
  Adder #(.width(32)) adder_2 (.a(pc_complete_1_pc_val), .out(adder_2_out));  // open: b, cin, cout
  instruction_stuct_decoder instruction_stuct_decoder_1 (
    .instruction(IR_q), .opcode(opcode), .rd(instruction_stuct_decoder_1_rd),
    .rs1(instruction_stuct_decoder_1_rs1), .rs2(instruction_stuct_decoder_1_rs2), .funct3(funct3),
    .funct7(funct7), .I_11_0(instruction_stuct_decoder_1_i_11_0));  // open: S_11_0, B_12_1_0, U_31_12, J_20_1_0
  Multiplexer #(.select(2), .width(5)) multiplexer_1 (
    .in1(instruction_stuct_decoder_1_rs1), .in2(instruction_stuct_decoder_1_rs2),
    .in3(instruction_stuct_decoder_1_rd), .out(out_1), .sel(S_r12d_A_GRG));  // open: in0
  PC_complete pc_complete_1 (
    .input_plus_1(adder_1_out), .input_plus_n(adder_2_out), .input_reset(pc_reset_val),
    .select_input(S_I_PC), .Write_enable(WE_PC), .Clock(CLK), .Pc_val(pc_complete_1_pc_val));  // open: in_4
  Multiplexer #(.width(32)) multiplexer_2 (
    .in0(pc_complete_1_pc_val), .in1(adder_3_out), .out(multiplexer_2_out), .sel(S_MA));
  Register #(.width(32)) MA (.D(multiplexer_2_out), .en(WE_MA), .clk(CLK), .Q(A_RAM));  // open: clr
  Adder #(.width(32)) adder_3 (
    .a(imm_Addr), .b(general_register_group_1_data_output), .out(adder_3_out));  // open: cin, cout
  general_register_group general_register_group_1 (
    .Address_5_bit(out_1), .Write_enbale(WE_GRG), .Output_enable(1'b1), .Clock(CLK),
    .Data_input(register_3_q), .Data_output(general_register_group_1_data_output));
  Multiplexer #(.width(32)) multiplexer_3 (
    .in0(O_RAM), .in1(general_register_group_1_data_output), .out(multiplexer_3_out), .sel(S_I_MD));
  Demultiplexer #(.width(32)) demultiplexer_1 (
    .out0(demultiplexer_1_out0), .out1(demultiplexer_1_out1), .in(general_register_group_1_data_output),
    .sel(S_AB_ALU));
  Register #(.width(32)) MD (.D(multiplexer_3_out), .en(WE_MD), .clk(CLK), .Q(MD_q));  // open: clr
  Demultiplexer #(.width(32)) demultiplexer_2 (.out0(I_RAM), .out1(demultiplexer_2_out1), .in(MD_q), .sel(S_O_MD));
  Register #(.width(32)) IR (.D(demultiplexer_2_out1), .en(WE_IR), .clk(CLLK), .Q(IR_q));  // open: clr
  Register #(.width(32)) register_1 (
    .D(demultiplexer_1_out0), .en(WE_A_ALU), .clk(CLK), .Q(register_1_q));  // open: clr
  Register #(.width(32)) register_2 (
    .D(demultiplexer_1_out1), .en(WE_B_ALU), .clk(CLK), .Q(register_2_q));  // open: clr
  ALU_complete alu_complete_1 (.A(register_1_q), .B(register_2_q), .op(op_ALU), .out_4(alu_complete_1_out_4));
  Register #(.width(32)) register_3 (
    .D(alu_complete_1_out_4), .en(WE_A_op_B), .clk(CLK), .Q(register_3_q));  // open: clr
  RAM #(.addrWidth(24), .dataWidth(32)) ram_1 (
    .addr(A_RAM[23:0]), .we(WE_RAM), .oe(OE_RAM), .clk(CLK), .din(I_RAM), .dout(O_RAM));
endmodule

module PC (
  input  [31:0] Pc_input,
  input  Write_enable,
  input  Clock,
  output [31:0] Pc_ouput
);

  Register #(.width(32)) register_1 (.D(Pc_input), .en(Write_enable), .clk(Clock), .Q(Pc_ouput));  // open: clr
endmodule

module PC_complete (
  input  [31:0] input_plus_1,
  input  [31:0] input_plus_n,
  input  [31:0] input_reset,
  input  [31:0] in_4,
  input  [1:0] select_input,
  input  Write_enable,
  input  Clock,
  output [31:0] Pc_val
);

  wire [31:0] multiplexer_1_out;

  Multiplexer #(.select(2), .width(32)) multiplexer_1 (
    .in0(input_plus_1), .in1(input_plus_n), .in2(input_reset), .in3(in_4), .out(multiplexer_1_out),
    .sel(select_input));
  PC pc_1 (.Pc_input(multiplexer_1_out), .Write_enable(Write_enable), .Clock(Clock), .Pc_ouput(Pc_val));
endmodule

module ALU (
  input  [31:0] A,
  input  [31:0] B,
  output [31:0] Carry,
  output [31:0] add,
  output [31:0] Borrow,
  output [31:0] subtract,
  output [31:0] shift_left_logic,
  output [31:0] shift_right_logic,
  output [31:0] shift_right_arithmetic,
  output [31:0] A_and_B,
  output [31:0] A_or_B,
  output [31:0] A_xor_B,
  output [31:0] slt,
  output [31:0] sltu
);

  wire adder_1_cout, comparator_1_lt, comparator_2_lt, subtractor_1_bout;

  Adder #(.width(32)) adder_1 (.a(A), .b(B), .out(add), .cin(1'b0), .cout(adder_1_cout));
  Subtractor #(.width(32)) subtractor_1 (.a(A), .b(B), .out(subtract), .bin(1'b0), .bout(subtractor_1_bout));
  Shifter #(.width(32)) shifter_1 (.in(A), .\dist (B[4:0]), .out(shift_left_logic));
  Shifter #(.shift("lr"), .width(32)) shifter_2 (.in(A), .\dist (B[4:0]), .out(shift_right_logic));
  Shifter #(.shift("ar"), .width(32)) shifter_3 (.in(A), .\dist (B[4:0]), .out(shift_right_arithmetic));
  assign A_and_B = A & B;  // AND_Gate and_1, 32 bits wide
  assign A_or_B = A | B;  // OR_Gate or_1, 32 bits wide
  assign A_xor_B = A ^ B;  // XOR_Gate xor_1, 32 bits wide
  Comparator #(.width(32)) comparator_1 (.a(A), .b(B), .lt(comparator_1_lt));  // open: gt, eq
  Comparator #(.mode("unsigned"), .width(32)) comparator_2 (.a(A), .b(B), .lt(comparator_2_lt));  // open: gt, eq
  Multiplexer #(.width(32)) multiplexer_1 (.in0({32{1'b0}}), .in1(32'h1), .out(Carry), .sel(adder_1_cout));
  Multiplexer #(.width(32)) multiplexer_2 (.in0({32{1'b0}}), .in1(32'h1), .out(Borrow), .sel(subtractor_1_bout));
  Multiplexer #(.width(32)) multiplexer_3 (.in0({32{1'b0}}), .in1(32'h1), .out(slt), .sel(comparator_1_lt));
  Multiplexer #(.width(32)) multiplexer_4 (.in0({32{1'b0}}), .in1(32'h1), .out(sltu), .sel(comparator_2_lt));
endmodule

module ALU_complete (
  input  [31:0] A,
  input  [31:0] B,
  input  [3:0] op,
  output [31:0] out_4
);

  wire decoder_1_out0, decoder_1_out1, decoder_1_out2, decoder_1_out3, decoder_1_out4, decoder_1_out5,
       decoder_1_out6, decoder_1_out7, decoder_1_out8, decoder_1_out9;
  wire [31:0] alu_1_a_and_b, alu_1_a_or_b, alu_1_a_xor_b, alu_1_add, alu_1_shift_left_logic,
       alu_1_shift_right_arithmetic, alu_1_shift_right_logic, alu_1_slt, alu_1_sltu, alu_1_subtract;

  Decoder #(.enable("false"), .select(4)) decoder_1 (
    .out0(decoder_1_out0), .out1(decoder_1_out1), .out2(decoder_1_out2), .out3(decoder_1_out3),
    .out4(decoder_1_out4), .out5(decoder_1_out5), .out6(decoder_1_out6), .out7(decoder_1_out7),
    .out8(decoder_1_out8), .out9(decoder_1_out9), .sel(op));  // open: out10, out11, out12, out13, out14, out15
  ALU alu_1 (
    .A(A), .B(B), .add(alu_1_add), .subtract(alu_1_subtract), .shift_left_logic(alu_1_shift_left_logic),
    .shift_right_logic(alu_1_shift_right_logic), .shift_right_arithmetic(alu_1_shift_right_arithmetic),
    .A_and_B(alu_1_a_and_b), .A_or_B(alu_1_a_or_b), .A_xor_B(alu_1_a_xor_b), .slt(alu_1_slt),
    .sltu(alu_1_sltu));  // open: Carry, Borrow
  assign out_4 = decoder_1_out9 ? alu_1_sltu : 32'bz;  // Controlled_Buffer controlled_buffer_1
  assign out_4 = decoder_1_out5 ? alu_1_a_and_b : 32'bz;  // Controlled_Buffer controlled_buffer_2
  assign out_4 = decoder_1_out6 ? alu_1_a_or_b : 32'bz;  // Controlled_Buffer controlled_buffer_3
  assign out_4 = decoder_1_out7 ? alu_1_a_xor_b : 32'bz;  // Controlled_Buffer controlled_buffer_4
  assign out_4 = decoder_1_out8 ? alu_1_slt : 32'bz;  // Controlled_Buffer controlled_buffer_5
  assign out_4 = decoder_1_out2 ? alu_1_shift_left_logic : 32'bz;  // Controlled_Buffer controlled_buffer_6
  assign out_4 = decoder_1_out3 ? alu_1_shift_right_logic : 32'bz;  // Controlled_Buffer controlled_buffer_7
  assign out_4 = decoder_1_out4 ? alu_1_shift_right_arithmetic : 32'bz;  // Controlled_Buffer controlled_buffer_8
  assign out_4 = decoder_1_out0 ? alu_1_add : 32'bz;  // Controlled_Buffer controlled_buffer_9
  assign out_4 = decoder_1_out1 ? alu_1_subtract : 32'bz;  // Controlled_Buffer controlled_buffer_10
endmodule

module general_register_group (
  input  [4:0] Address_5_bit,
  input  Write_enbale,
  input  Output_enable,
  input  Clock,
  input  [31:0] Data_input,
  output [31:0] Data_output
);

  RAM #(.addrWidth(5), .dataWidth(32)) Register_group (
    .addr(Address_5_bit), .we(Write_enbale), .oe(Output_enable), .clk(Clock), .din(Data_input),
    .dout(Data_output));
endmodule

module instruction_stuct_decoder (
  input  [31:0] instruction,
  output [6:0] opcode,
  output [4:0] rd,
  output [4:0] rs1,
  output [4:0] rs2,
  output [2:0] funct3,
  output [6:0] funct7,
  output [11:0] I_11_0,
  output [11:0] S_11_0,
  output [12:0] B_12_1_0,
  output [19:0] U_31_12,
  output [12:0] J_20_1_0
);


  assign B_12_1_0 = {instruction[31], instruction[7], instruction[30:25], instruction[11:8], 1'b0};
  assign funct3 = instruction[14:12];
  assign funct7 = instruction[31:25];
  assign I_11_0 = instruction[31:20];
  assign opcode = instruction[6:0];
  assign rd = instruction[11:7];
  assign rs1 = instruction[19:15];
  assign rs2 = instruction[24:20];
  assign S_11_0 = {instruction[31:25], instruction[11:7]};
  assign U_31_12 = instruction[31:12];
endmodule

module Instruction_to_Sequence (
  input  Clock,
  input  Clear_asyn,
  input  [6:0] opcode,
  input  [2:0] funct3,
  input  [6:0] funct7,
  output [1:0] S_r12d_A_GRG,
  output WE_GRG,
  output S_AB_ALU,
  output WE_A_ALU,
  output WE_B_ALU,
  output WE_A_op_B,
  output [3:0] add
);

  wire and_1_out, and_2_out, comparator_1_eq, comparator_2_eq, decoder_opcode_1_r;

  decoder_opcode decoder_opcode_1 (
    .opcode(opcode), .R(decoder_opcode_1_r));  // open: I_R, B, I_L, S, J, I_J, U_lui, U_auipc
  and and_1 (and_1_out, Clock, decoder_opcode_1_r);
  R_type_instruction_sequence r_type_instruction_sequence_1 (
    .Clock(and_1_out), .Clear_asyn(Clear_asyn), .S_r12d_A_GRG(S_r12d_A_GRG), .WE_GRG(WE_GRG),
    .S_AB_ALU(S_AB_ALU), .WE_A_ALU(WE_A_ALU), .WE_B_ALU(WE_B_ALU), .WE_A_op_B(WE_A_op_B));  // open: Output_Counter
  Comparator #(.mode("unsigned"), .width(3)) comparator_1 (
    .a(funct3), .b(3'b000), .eq(comparator_1_eq));  // open: gt, lt
  Comparator #(.mode("unsigned"), .width(7)) comparator_2 (
    .a(funct7), .b({7{1'b0}}), .eq(comparator_2_eq));  // open: gt, lt
  and and_2 (and_2_out, comparator_1_eq, comparator_2_eq);
  assign add = and_2_out ? 4'b0000 : 4'bz;  // Controlled_Buffer controlled_buffer_1
endmodule

module counter_16 (
  input  WE,
  input  Clock,
  input  Clear_asyn,
  output Carry,
  output [3:0] Output_counter
);

  wire [3:0] adder_1_out;

  Register #(.trigger("falling"), .width(4)) register_1 (
    .D(adder_1_out), .en(WE), .clk(Clock), .Q(Output_counter), .clr(Clear_asyn));
  Adder #(.width(4)) adder_1 (.a(Output_counter), .b(4'b0001), .out(adder_1_out), .cin(1'b0), .cout(Carry));
endmodule

module counter_10 (
  input  WE,
  input  Clock,
  input  Clear_asyn,
  output [3:0] Ouput_Counter,
  output Carry
);

  wire and_1_out, or_1_out;

  or or_1 (or_1_out, Clear_asyn, and_1_out);
  counter_16 counter_16_1 (
    .WE(WE), .Clock(Clock), .Clear_asyn(or_1_out), .Output_counter(Ouput_Counter));  // open: Carry
  and and_1 (and_1_out, Ouput_Counter[3], Ouput_Counter[1]);
  and and_2 (Carry, Ouput_Counter[0], Ouput_Counter[3]);
endmodule

module counter_any_22 (
  input  WE,
  input  Clock,
  output [7:0] Output_Counter,
  output Carry
);

  wire and_1_out, and_2_out;

  and and_1 (and_1_out, Output_Counter[1], Output_Counter[5], Output_Counter[0]);
  counter_10 counter_10_1 (
    .WE(WE), .Clock(Clock), .Clear_asyn(and_1_out), .Ouput_Counter(Output_Counter[3:0]));  // open: Carry
  and and_2 (and_2_out, Output_Counter[1], Output_Counter[3]);
  counter_10 counter_10_2 (
    .WE(WE), .Clock(and_2_out), .Clear_asyn(and_1_out), .Ouput_Counter(Output_Counter[7:4]));  // open: Carry
  and and_3 (Carry, Output_Counter[5], Output_Counter[1]);
endmodule

module counter_8 (
  input  WE,
  input  Clock,
  input  Clear_asyn,
  output [3:0] Output_counter,
  output Carry_counter
);

  wire or_1_out;

  or or_1 (or_1_out, Clear_asyn, Output_counter[3]);
  counter_16 counter_16_1 (
    .WE(WE), .Clock(Clock), .Clear_asyn(or_1_out), .Output_counter(Output_counter));  // open: Carry
  and and_1 (Carry_counter, Output_counter[1], Output_counter[0], Output_counter[2]);
endmodule

module R_type_logic_sequence (
  input  Clock,
  input  Clear,
  output Q6,
  output Q5,
  output Q4,
  output Q3,
  output Q2,
  output Q1,
  output Q0
);

  wire and_1_out, and_2_out, and_3_out, and_4_out, and_5_out, and_6_out, and_7_out, and_8_out, and_9_out,
       and_10_out, and_11_out, and_12_out, and_13_out, not_1_out, not_2_out, not_3_out, not_4_out, not_5_out,
       not_6_out, not_7_out, not_8_out, or_1_out, or_2_out;

  D_Flip_Flop d_ff_1 (.D(or_1_out), .clk(not_1_out), .Q(Q6), .reset(Clear));  // open: Qn, preset
  D_Flip_Flop d_ff_2 (.D(or_2_out), .clk(not_1_out), .Q(Q5), .reset(Clear));  // open: Qn, preset
  D_Flip_Flop d_ff_3 (.D(and_9_out), .clk(not_1_out), .Q(Q4), .reset(Clear));  // open: Qn, preset
  D_Flip_Flop d_ff_4 (.D(and_10_out), .clk(not_1_out), .Q(Q3), .reset(Clear));  // open: Qn, preset
  D_Flip_Flop d_ff_5 (.D(and_11_out), .clk(not_1_out), .Q(Q2), .reset(Clear));  // open: Qn, preset
  D_Flip_Flop d_ff_6 (.D(and_12_out), .clk(not_1_out), .Q(Q1), .reset(Clear));  // open: Qn, preset
  D_Flip_Flop d_ff_7 (.D(and_13_out), .clk(not_1_out), .Q(Q0), .reset(Clear));  // open: Qn, preset
  not not_1 (not_1_out, Clock);
  not not_2 (not_2_out, Q6);
  not not_3 (not_3_out, Q5);
  not not_4 (not_4_out, Q4);
  not not_5 (not_5_out, Q3);
  not not_6 (not_6_out, Q2);
  not not_7 (not_7_out, Q1);
  not not_8 (not_8_out, Q0);
  and and_1 (and_1_out, not_2_out, Q5, not_4_out, not_5_out, Q2, not_7_out, not_8_out);
  and and_2 (and_2_out, Q6, not_3_out, not_4_out, not_5_out, not_6_out, not_7_out, not_8_out);
  and and_3 (and_3_out, Q6, not_3_out, not_4_out, Q3, not_6_out, Q1, not_8_out);
  and and_4 (and_4_out, Q6, Q5, not_4_out, not_5_out, not_6_out, not_7_out, Q0);
  and and_5 (and_5_out, not_2_out, not_3_out, not_4_out, not_5_out, not_6_out, not_7_out, not_8_out);
  and and_6 (and_6_out, not_2_out, Q5, not_4_out, not_5_out, not_6_out, not_7_out, not_8_out);
  and and_7 (and_7_out, Q6, not_3_out, not_4_out, Q3, not_6_out, Q1, not_8_out);
  and and_8 (and_8_out, Q6, Q5, not_4_out, not_5_out, not_6_out, not_7_out, Q0);
  and and_9 (and_9_out, Q6, Q5, not_4_out, not_5_out, not_6_out, not_7_out, Q0);
  and and_10 (and_10_out, Q6, not_3_out, not_4_out, not_5_out, not_6_out, not_7_out, not_8_out);
  and and_11 (and_11_out, not_2_out, Q5, not_4_out, not_5_out, not_6_out, not_7_out, not_8_out);
  and and_12 (and_12_out, Q6, not_3_out, not_4_out, not_5_out, not_6_out, not_7_out, not_8_out);
  and and_13 (and_13_out, Q6, not_3_out, not_4_out, Q3, not_6_out, Q1, not_8_out);
  or or_1 (or_1_out, and_1_out, and_2_out, and_3_out, and_4_out);
  or or_2 (or_2_out, and_5_out, and_6_out, and_7_out, and_8_out);
endmodule

module R_type_instruction_sequence (
  input  Clock,
  input  Clear_asyn,
  output [3:0] Output_Counter,
  output [1:0] S_r12d_A_GRG,
  output WE_GRG,
  output S_AB_ALU,
  output WE_A_ALU,
  output WE_B_ALU,
  output WE_A_op_B
);

  wire and_1_out, counter_8_1_carry_counter, not_1_out, s_r_ff_1_q;

  counter_8 counter_8_1 (
    .WE(1'b1), .Clock(Clock), .Clear_asyn(Clear_asyn), .Output_counter(Output_Counter),
    .Carry_counter(counter_8_1_carry_counter));
  S_R_Flip_Flop s_r_ff_1 (
    .S(1'b1), .R(1'b0), .clk(counter_8_1_carry_counter), .Q(s_r_ff_1_q), .reset(Clear_asyn));  // open: Qn, preset
  not not_1 (not_1_out, s_r_ff_1_q);
  and and_1 (and_1_out, Clock, not_1_out);
  R_type_logic_sequence r_type_logic_sequence_1 (
    .Clock(and_1_out), .Clear(Clear_asyn), .Q6(S_r12d_A_GRG[1]), .Q5(S_r12d_A_GRG[0]), .Q4(WE_GRG),
    .Q3(S_AB_ALU), .Q2(WE_A_ALU), .Q1(WE_B_ALU), .Q0(WE_A_op_B));
endmodule

module decoder_opcode (
  input  [6:0] opcode,
  output R,
  output I_R,
  output B,
  output I_L,
  output S,
  output J,
  output I_J,
  output U_lui,
  output U_auipc
);

  Comparator #(.mode("unsigned"), .width(7)) comparator_1 (.a(opcode), .b(7'b0110011), .eq(R));  // open: gt, lt
  Comparator #(.mode("unsigned"), .width(7)) comparator_2 (.a(opcode), .b(7'b0010011), .eq(I_R));  // open: gt, lt
  Comparator #(.mode("unsigned"), .width(7)) comparator_3 (.a(opcode), .b(7'b1100011), .eq(B));  // open: gt, lt
  Comparator #(.mode("unsigned"), .width(7)) comparator_4 (.a(opcode), .b(7'b0000011), .eq(I_L));  // open: gt, lt
  Comparator #(.mode("unsigned"), .width(7)) comparator_5 (.a(opcode), .b(7'b0100011), .eq(S));  // open: gt, lt
  Comparator #(.mode("unsigned"), .width(7)) comparator_6 (.a(opcode), .b(7'b1101111), .eq(J));  // open: gt, lt
  Comparator #(.mode("unsigned"), .width(7)) comparator_7 (.a(opcode), .b(7'b1100111), .eq(I_J));  // open: gt, lt
  Comparator #(.mode("unsigned"), .width(7)) comparator_8 (.a(opcode), .b(7'b0110111), .eq(U_lui));  // open: gt, lt
  Comparator #(.mode("unsigned"), .width(7)) comparator_9 (.a(opcode), .b(7'b0010111), .eq(U_auipc));  // open: gt, lt
endmodule
